# Fritzing sketch GENIUS (saved by Fritzing 0.9.3b)
circuit board: 6.88566cm x 5.36311cm
breadboards: 1

parts:
  LED1 = smd LED [color="Red (633nm)" package="1206 [SMD]"]
  R1 = Resistor [tolerance=±5% resistance=220 package="1206 [SMD]"]
  LED2 = smd LED [color="Green (555nm)" package="1206 [SMD]"]
  R2 = Resistor [tolerance=±5% resistance=220 package="1206 [SMD]"]
  S2 = Pushbutton [package="[SMD]"]
  LED3 = smd LED [color="Blue (430nm)" package="1206 [SMD]"]
  R3 = Resistor [tolerance=±5% resistance=220 package="1206 [SMD]"]
  S3 = Pushbutton [package="[SMD]"]
  LED4 = smd LED [color="Yellow (595nm)" package="1206 [SMD]"]
  R4 = Resistor [tolerance=±5% resistance=220 package="1206 [SMD]"]
  S4 = Pushbutton [package="[SMD]"]
  S1 = Pushbutton [package="[SMD]"]
  Componente1 = Arduino Uno (Rev3)
  J1 = Piezo Speaker

nets:
  N1: LED1.cathode, R1.Pin_0
  N2: LED1.anode, Componente1.D8
  N3: R1.Pin_1, R2.Pin_1, S2.Pin_3, S2.Pin_4, R3.Pin_1, S3.Pin_3, S3.Pin_4, R4.Pin_1, S4.Pin_3, S4.Pin_4, S1.Pin_3, S1.Pin_4, Componente1.GND, J1.pin1
  N4: LED2.cathode, R2.Pin_0
  N5: LED2.anode, Componente1.D9_PWM
  N6: S2.Pin_1, S2.Pin_2, Componente1.D3_PWM
  N7: LED3.cathode, R3.Pin_0
  N8: LED3.anode, Componente1.D10_PWM/SS
  N9: S3.Pin_1, S3.Pin_2, Componente1.D4
  N10: LED4.cathode, R4.Pin_0
  N11: LED4.anode, Componente1.D11_PWM/MOSI
  N12: S4.Pin_1, S4.Pin_2, Componente1.D5_PWM
  N13: S1.Pin_1, S1.Pin_2, Componente1.D2
  N14: Componente1.D13/SCK, J1.pin2

notes:
  Powered By Decade Technologies

// code stored in the sketch: GENIUS.ino
#define RED_BUTTON 2
#define GREEN_BUTTON 3
#define BLUE_BUTTON 4
#define YELLOW_BUTTON 5

#define RED_LED 8
#define GREEN_LED 9
#define BLUE_LED 10
#define YELLOW_LED 11

#define DEFAULT_BUZZER 13

const int MAX_SEQUENCE = 4;
const int HOLD_ON = 500;
const int UNDEFINIED = -1;

int gameSet[MAX_SEQUENCE];
int roundPlayer;
int rightAnswer;

enum statusGame {
  READY_TO_PLAY
, WAITING_RESPONSE
, YOU_WIN
, GAME_OVER
};

void setPlayTone(int frequence, int duration) {
  tone(DEFAULT_BUZZER, frequence, duration);
}

void setFlashLight(int ledPort, int waitingTime) {
  digitalWrite(ledPort, HIGH);
  delay(waitingTime);

  digitalWrite(ledPort, LOW);
  delay(waitingTime);
}

int getButtonPressed() {
  if (digitalRead(RED_BUTTON) == LOW) {
    setFlashLight(RED_LED, HOLD_ON);

    return RED_LED;
  }

  if (digitalRead(GREEN_BUTTON) == LOW) {
    setFlashLight(GREEN_LED, HOLD_ON);

    return GREEN_LED;
  }

  if (digitalRead(BLUE_BUTTON) == LOW) {
    setFlashLight(BLUE_LED, HOLD_ON);

    return BLUE_LED;
  }

  if (digitalRead(YELLOW_BUTTON) == LOW) {
    setFlashLight(YELLOW_LED, HOLD_ON);

    return YELLOW_LED;
  }

  return UNDEFINIED;
}

void playRoundSequence() {
  for (int i = 0; i < roundPlayer; i++) {
    setFlashLight(gameSet[i], HOLD_ON);
  }
}

void setRoundPlayer() {
  roundPlayer++;
  rightAnswer = 0;

  if (roundPlayer <= MAX_SEQUENCE) {
    playRoundSequence();
  }
}

void setRightAnswer() {
  int answer = getButtonPressed();

  if (answer == UNDEFINIED) {
    return;
  }

  if (answer == gameSet[rightAnswer]) {
    rightAnswer++;
  } else {
    roundPlayer = MAX_SEQUENCE + 2;
  }
}

int getStatusGame() {
  if (roundPlayer <= MAX_SEQUENCE) {
    if (rightAnswer == roundPlayer) {
      return READY_TO_PLAY;
    } else {
      return WAITING_RESPONSE;
    }
  } else if (roundPlayer == MAX_SEQUENCE + 1) {
    return YOU_WIN;
  } else {
    return GAME_OVER;
  }
}

void welcome() {
  digitalWrite(RED_LED, HIGH);
  digitalWrite(GREEN_LED, HIGH);
  digitalWrite(BLUE_LED, HIGH);
  digitalWrite(YELLOW_LED, HIGH);

  delay(400);

  digitalWrite(RED_LED, LOW);
  digitalWrite(GREEN_LED, LOW);
  digitalWrite(BLUE_LED, LOW);
  digitalWrite(YELLOW_LED, LOW);

  delay(400);
}


void congratulation() {
  for (int i = 0; i < MAX_SEQUENCE + 1; i++) {
    setFlashLight(gameSet[i], 200);
  }

  newGame();
}

void fail() {
  setPlayTone(2048, 256);

  digitalWrite(RED_LED, HIGH);
  digitalWrite(GREEN_LED, HIGH);
  digitalWrite(BLUE_LED, HIGH);
  digitalWrite(YELLOW_LED, HIGH);

  delay(300);

  newGame();
}

void newGame() {
  roundPlayer = 0;
  rightAnswer = 0;

  randomSeed(analogRead(0));

  for (int i = 0; i < MAX_SEQUENCE; i++) {
    gameSet[i] = random(RED_LED, YELLOW_LED + 1);
  }

  welcome();
}

void setup() {
  //Serial.begin(9600);

  pinMode(RED_BUTTON, INPUT_PULLUP);
  pinMode(GREEN_BUTTON, INPUT_PULLUP);
  pinMode(BLUE_BUTTON, INPUT_PULLUP);
  pinMode(YELLOW_BUTTON, INPUT_PULLUP);

  pinMode(RED_LED, OUTPUT);
  pinMode(GREEN_LED, OUTPUT);
  pinMode(BLUE_LED, OUTPUT);
  pinMode(YELLOW_LED, OUTPUT);

  pinMode(DEFAULT_BUZZER, OUTPUT);

  newGame();
}

void loop() {
  switch (getStatusGame()) {
    case READY_TO_PLAY:
      //Serial.println("READY_TO_PLAY");

      setRoundPlayer();
      break;
    case WAITING_RESPONSE:
      //Serial.println("WAITING_RESPONSE");

      setRightAnswer();
      break;
    case YOU_WIN:
      //Serial.println("YOU_WIN");

      congratulation();
      break;
    case GAME_OVER:
      //Serial.println("GAME_OVER");

      fail();
      break;
  }
}

// code stored in the sketch: GENIUSv1.ino
#define RED_BUTTON 2
#define GREEN_BUTTON 3
#define BLUE_BUTTON 4
#define YELLOW_BUTTON 5

#define RED_LED 8
#define GREEN_LED 9
#define BLUE_LED 10
#define YELLOW_LED 11

#define DEFAULT_BUZZER 13

const int MAX_SEQUENCE = 4;
const int HOLD_ON = 500;
const int UNDEFINIED = -1;

int gameSet[MAX_SEQUENCE];
int roundPlayer;
int rightAnswer;

enum statusGame {
  READY_TO_PLAY
, WAITING_RESPONSE
, YOU_WIN
, GAME_OVER
};

void setPlayTone(int frequence, int duration) {
  tone(DEFAULT_BUZZER, frequence, duration);
}

void setFlashLight(int ledPort, int waitingTime) {
  digitalWrite(ledPort, HIGH);
  delay(waitingTime);

  setPlayTone(ledPort * 512, 128);

  digitalWrite(ledPort, LOW);
  delay(waitingTime);
}

int getButtonPressed() {
  if (digitalRead(RED_BUTTON) == LOW) {
    setFlashLight(RED_LED, HOLD_ON);

    return RED_LED;
  }

  if (digitalRead(GREEN_BUTTON) == LOW) {
    setFlashLight(GREEN_LED, HOLD_ON);

    return GREEN_LED;
  }

  if (digitalRead(BLUE_BUTTON) == LOW) {
    setFlashLight(BLUE_LED, HOLD_ON);

    return BLUE_LED;
  }

  if (digitalRead(YELLOW_BUTTON) == LOW) {
    setFlashLight(YELLOW_LED, HOLD_ON);

    return YELLOW_LED;
  }

  return UNDEFINIED;
}

void playRoundSequence() {
  for (int i = 0; i < roundPlayer; i++) {
    setFlashLight(gameSet[i], HOLD_ON);
  }
}

void setRoundPlayer() {
  roundPlayer++;
  rightAnswer = 0;

  if (roundPlayer <= MAX_SEQUENCE) {
    playRoundSequence();
  }
}

void setRightAnswer() {
  int answer = getButtonPressed();

  if (answer == UNDEFINIED) {
    return;
  }

  if (answer == gameSet[rightAnswer]) {
    rightAnswer++;
  } else {
    roundPlayer = MAX_SEQUENCE + 2;
  }
}

int getStatusGame() {
  if (roundPlayer <= MAX_SEQUENCE) {
    if (rightAnswer == roundPlayer) {
      return READY_TO_PLAY;
    } else {
      return WAITING_RESPONSE;
    }
  } else if (roundPlayer == MAX_SEQUENCE + 1) {
    return YOU_WIN;
  } else {
    return GAME_OVER;
  }
}

void welcome() {
  digitalWrite(RED_LED, HIGH);
  digitalWrite(GREEN_LED, HIGH);
  digitalWrite(BLUE_LED, HIGH);
  digitalWrite(YELLOW_LED, HIGH);

  delay(400);

  digitalWrite(RED_LED, LOW);
  digitalWrite(GREEN_LED, LOW);
  digitalWrite(BLUE_LED, LOW);
  digitalWrite(YELLOW_LED, LOW);

  delay(400);
}



void congratulation() {
  for (int i = 0; i < MAX_SEQUENCE + 1; i++) {
    setFlashLight(gameSet[i], 200);
  }

  newGame();
}

void fail() {
  setPlayTone(2048, 256);

  digitalWrite(RED_LED, HIGH);
  digitalWrite(GREEN_LED, HIGH);
  digitalWrite(BLUE_LED, HIGH);
  digitalWrite(YELLOW_LED, HIGH);

  delay(300);

  newGame();
}

void newGame() {
  roundPlayer = 0;
  rightAnswer = 0;

  randomSeed(analogRead(0));

  for (int i = 0; i < MAX_SEQUENCE; i++) {
    gameSet[i] = random(RED_LED, YELLOW_LED + 1);
  }

  welcome();
}

void setup() {
  //Serial.begin(9600);

  pinMode(RED_BUTTON, INPUT_PULLUP);
  pinMode(GREEN_BUTTON, INPUT_PULLUP);
  pinMode(BLUE_BUTTON, INPUT_PULLUP);
  pinMode(YELLOW_BUTTON, INPUT_PULLUP);

  pinMode(RED_LED, OUTPUT);
  pinMode(GREEN_LED, OUTPUT);
  pinMode(BLUE_LED, OUTPUT);
  pinMode(YELLOW_LED, OUTPUT);

  pinMode(DEFAULT_BUZZER, OUTPUT);

  newGame();
}

void loop() {
  switch (getStatusGame()) {
    case READY_TO_PLAY:
      //Serial.println("READY_TO_PLAY");

      setRoundPlayer();
      break;
    case WAITING_RESPONSE:
      //Serial.println("WAITING_RESPONSE");

      setRightAnswer();
      break;
    case YOU_WIN:
      //Serial.println("YOU_WIN");

      congratulation();
      break;
    case GAME_OVER:
      //Serial.println("GAME_OVER");

      fail();
      break;
  }
}
